# Fritzing sketch Circuito-Desmitificando (saved by Fritzing 0.9.2b)
breadboards: 1

parts:
  SW1 = DIP Switch 8 Position [package=dipswitch-08]
  R1 = Resistor [tolerance=±5% resistance=10k package=THT]
  R2 = Resistor [tolerance=±5% resistance=10k package=THT]
  R3 = Resistor [tolerance=±5% resistance=10k package=THT]
  R4 = Resistor [tolerance=±5% resistance=220 package=THT]

nets:
  5V: SW1.1, SW1.2, SW1.3, SW1.4
  N1: SW1.13, R4.Pin_0
  N2: SW1.14, R3.Pin_0
  N3: SW1.15, R2.Pin_0
  N4: SW1.16, R1.Pin_0
  GND: R1.Pin_1, R2.Pin_1, R3.Pin_1, R4.Pin_1
