# Fritzing sketch Entrada-Resistencia_pull_down (saved by Fritzing 0.9.2b)
breadboards: 1

parts:
  SW1 = DIP SWITCH [package=dipswitch-02]
  R1 = Resistor [tolerance=±5% resistance=10k package=THT]

nets:
  5V: SW1.1
  Output: SW1.4, R1.Pin_0
  GND: R1.Pin_1

notes:
  Salida Lógica
  Salida Logica
