# Fritzing sketch Transistor_y_LED (saved by Fritzing 0.9.2b)
breadboards: 1

parts:
  R1 = Resistor [tolerance=±5% resistance=22k package=THT]
  Q1 = NPN-Transistor [package="TO92 [THT]"]
  R2 = Resistor [tolerance=±5% resistance=220k package=THT]
  LED1 = LED - 5mm [color="Green (570nm)" package="5 mm [THT]"]
  R3 = Resistor [tolerance=±5% resistance=220 package=THT]

nets:
  Entrada Lógica: R1.Pin_0
  N1: R1.Pin_1, Q1.B, R2.Pin_0
  GND: Q1.E, R2.Pin_1
  N2: Q1.C, LED1.cathode
  N3: LED1.anode, R3.Pin_1
  5V: R3.Pin_0

notes:
  Entrada Lógica
