# Fritzing sketch ad2-de0_nano_soc (saved by Fritzing 0.9.3b)

parts:
  Analog_Discovery_2 = Analog Discovery 2: USB Oscilloscope [part_number=410-321 package=THT]
  GPIO_0 = DE0-Nano-SoC GPIO [form="♂ (shrouded male)" package=THT]

nets:
  GND: Analog_Discovery_2.GND, GPIO_0.pin12
  N1: Analog_Discovery_2.0, GPIO_0.pin1
  N2: Analog_Discovery_2.1, GPIO_0.pin2
  N3: Analog_Discovery_2.2, GPIO_0.pin3
  N4: Analog_Discovery_2.3, GPIO_0.pin4
  N5: Analog_Discovery_2.4, GPIO_0.pin5
  N6: Analog_Discovery_2.5, GPIO_0.pin6
  N7: Analog_Discovery_2.6, GPIO_0.pin7
  N8: Analog_Discovery_2.7, GPIO_0.pin8
  N9: Analog_Discovery_2.8, GPIO_0.pin9
  N10: Analog_Discovery_2.9, GPIO_0.pin10
  N11: Analog_Discovery_2.10, GPIO_0.pin13
  N12: Analog_Discovery_2.11, GPIO_0.pin14
  N13: Analog_Discovery_2.12, GPIO_0.pin15
  N14: Analog_Discovery_2.13, GPIO_0.pin16
  N15: Analog_Discovery_2.14, GPIO_0.pin17
  N16: Analog_Discovery_2.15, GPIO_0.pin18

custom parts:
  Analog Discovery 2: USB Oscilloscope: The Analog Discovery 2 is a portable, usb connected labratory for every engineer. It contains the benchtop tools necessary for both analog and digital projects. It has an Oscilloscope, Arbritary Waveform Generator, Power Supplies, Static Digital I/O, Pattern Generator, Logic Analyzer, Network Analyzer, Spectrum Analyzer, Data Logger, and Script Editor
  DE0-Nano-SoC GPIO: Terasic 2x20 GPIO Header
